// Logisim project alu.circ as structural Verilog: 1 circuit, main circuit ALU
module ALU (
  input  [31:0] A,
  input  [31:0] B,
  input  [3:0] ALU_Op,
  output [31:0] Out
);

  wire slt;
  wire [31:0] add, \and , div, mul, mulh, \or , rem, sll, slr, sub, \xor ;

  Shifter #(.width(32)) shifter_1 (.in(A), .\dist (B[4:0]), .out(sll));
  Shifter #(.width(32), .shift("lr")) shifter_2 (.in(A), .\dist (B[4:0]), .out(slr));
  Adder #(.width(32)) adder_1 (.a(A), .b(B), .out(add));  // open: cin, cout
  assign \and  = A & B;  // AND_Gate and_1, 32 bits wide
  assign \or  = A | B;  // OR_Gate or_1, 32 bits wide
  assign \xor  = A ^ B;  // XOR_Gate xor_1, 32 bits wide
  Comparator #(.width(32)) comparator_1 (.a(A), .b(B), .lt(slt));  // open: gt, eq
  Multiplier #(.width(32)) multiplier_1 (.a(A), .b(B), .out(mul), .cout(mulh));  // open: cin
  Divider #(.width(32)) divider_1 (.a(A), .b(B), .out(div), .rem(rem));  // open: upper
  Subtractor #(.width(32)) subtractor_1 (.a(A), .b(B), .out(sub));  // open: bin, bout
  Multiplexer #(.select(4), .width(32)) multiplexer_1 (
    .in0(sll), .in1(slr), .in2(add), .in3(\and ), .in4(\or ), .in5(\xor ), .in6({{31{1'b0}}, slt}),
    .in7(mul), .in8(mulh), .in9(div), .in10(rem), .in11(sub), .out(Out), .sel(ALU_Op));  // open: in12, in13, in14, in15, en

  // Other names for the same wires on the sheet: B_4_0[4:0] = B[4:0]; Op[3:0] = ALU_Op

  // Notes on the sheet:
  //   Inputs
  //   NOTE
  //   Please do not modify/replace/move/change/delete/etc input and output pins
  //   Outputs
endmodule
