// Logisim project regfile.circ as structural Verilog: 1 circuit, main circuit RegFile
module RegFile (
  input  [4:0] RD,
  input  [4:0] RS1,
  input  [4:0] RS2,
  input  [31:0] W,
  input  WE,
  input  Clk,
  output [31:0] s0,
  output [31:0] s1,
  output [31:0] t0,
  output [31:0] t1,
  output [31:0] a0,
  output [31:0] ra,
  output [31:0] sp,
  output [31:0] R1,
  output [31:0] R2
);

  wire undriven;

  Register #(.width(32)) zero (.en(1'b0), .clr(undriven));  // open: D, Q, clk
  Register #(.width(32)) u_ra (.D(W), .clk(Clk));  // open: en, Q, clr
  Register #(.width(32)) u_sp (.D(W), .clk(Clk));  // open: en, Q, clr
  Register #(.width(32)) u_t0 (.D(W), .clk(Clk));  // open: en, Q, clr
  Register #(.width(32)) u_t1 (.D(W), .clk(Clk));  // open: en, Q, clr
  Register #(.width(32)) u_s0 (.D(W), .clk(Clk));  // open: en, Q, clr
  Register #(.width(32)) u_s1 (.D(W), .clk(Clk));  // open: en, Q, clr
  Register #(.width(32)) u_a0 (.D(W), .clk(Clk));  // open: en, Q, clr
  Register #(.width(32)) a1 (.D(W), .clk(Clk));  // open: en, Q, clr

  // Notes on the sheet:
  //   Write Register
  //   Read Register 1
  //   Read Register 2
  //   Write Data
  //   Write Enable
  //   Clock
  //   NOTE
  //   Please do not modify/replace/move/change/delete/etc input and output pins
  //   These are debug/test outputs from your circuit
  //   Read Data 1
  //   Read Data 2
endmodule
